# Fritzing sketch My favourite color is glitter - perfboard (saved by Fritzing 0.9.10b)
stripboards: 1

parts:
  Part1 = Arduino Nano (Rev3.0)
  U1 = POT [knob_status=50% power=0.5W package=pot_mammoth]
  R6 = Resistor [tolerance=±5% power=0.25 resistance=2.2k package=THT]
  R10 = Resistor [tolerance=±5% power=0.25 resistance=2.2k package=THT]
  U2 = POT [knob_status=50% power=0.5W package=pot_mammoth]
  U4 = POT [knob_status=50% power=0.5W package=pot_mammoth]
  J2 = Camdenboss CTB0158-2 [part_number=CTB0158-2 package=THT]  # not connected
  J3 = Camdenboss CTB0158-2 [part_number=CTB0158-2 package=THT]  # not connected
  J4 = Camdenboss CTB0158-2 [part_number=CTB0158-2 package=THT]  # not connected
  J5 = Camdenboss CTB0158-2 [part_number=CTB0158-2 package=THT]  # not connected
  J6 = Camdenboss CTB0158-2 [part_number=CTB0158-2 package=THT]  # not connected
  J7 = Camdenboss CTB0158-2 [part_number=CTB0158-2 package=THT]  # not connected
  J8 = Camdenboss CTB0158-2 [part_number=CTB0158-2 package=THT]
  J9 = Camdenboss CTB0158-2 [part_number=CTB0158-2 package=THT]
  J10 = Camdenboss CTB0158-2 [part_number=CTB0158-2 package=THT]  # not connected
  J11 = Camdenboss CTB0158-2 [part_number=CTB0158-2 package=THT]  # not connected
  J12 = Camdenboss CTB0158-2 [part_number=CTB0158-2 package=THT]  # not connected
  J13 = Camdenboss CTB0158-2 [part_number=CTB0158-2 package=THT]  # not connected
  HC-SR04_Sensor_1 = HC-SR04 Ultrasonic Distance Sensor
  J1 = Basic Servo

nets:
  GND: Part1.GND, U1.A, R10.Pin_1, U2.A, U4.A, J8.pin1, HC-SR04_Sensor_1.GND, J1.gnd
  N1: Part1.D4, HC-SR04_Sensor_1.ECHO
  N2: Part1.D5, HC-SR04_Sensor_1.TRIG
  N3: Part1.D9, J9.pin2, J1.pulse
  VCC: Part1.5V, U1.E, U2.E, U4.E, J8.pin2, HC-SR04_Sensor_1.VCC, J1.vcc
  N4: Part1.A6, U4.S
  N5: Part1.A5, U2.S
  N6: Part1.A4, U1.S
  N7: Part1.A3, R10.Pin_0
  N8: Part1.A1, R6.Pin_0
