# Fritzing sketch TMC2209 hello world without libraries (saved by Fritzing 1.0.6)
breadboards: 1

parts:
  BIGTREETECH_TMC2209_V1_1 = TMC2209
  J1 = Power Jack [package=power_jack_combo]
  Part1 = Arduino Nano (Rev3.0) (ICSP)  # not connected
  M1 = Stepper Motor - Unipolar
  C1 = Electrolytic Capacitor [capacitance=1µF voltage=35V package="100 mil [THT, electrolytic]"]

nets:
  N1: BIGTREETECH_TMC2209_V1_1.VM, J1.GND, C1.+
  N2: BIGTREETECH_TMC2209_V1_1.OUT_B2, M1.D
  N3: BIGTREETECH_TMC2209_V1_1.OUT_A2, M1.A
  N4: BIGTREETECH_TMC2209_V1_1.OUT_A1, M1.B
  N5: BIGTREETECH_TMC2209_V1_1.OUT_B1, M1.C
  N6: J1.GNDBREAK, C1.-

notes:
  9-12V

custom parts:
  TMC2209: This is a Stepper Motor Controller for integrated circuits.
