# Fritzing sketch My favourite color is glitter - Sonar + SONY front setup (saved by Fritzing 0.9.9b)
breadboards: 1

parts:
  Part1 = Arduino Nano (Rev3.0)
  Sw1 = SS13D01
  R1 = Resistor [tolerance=±5% power=0.25 resistance=220 package=THT]
  R2 = Resistor [tolerance=±5% power=0.25 resistance=220 package=THT]
  R3 = Resistor [tolerance=±5% power=0.25 resistance=220 package=THT]
  R4 = Resistor [tolerance=±5% power=0.25 resistance=2.2k package=THT]
  U1 = POT [knob_status=50% power=0.5W package=pot_mammoth]
  HC-SR04_Sensor_1 = HC-SR04 Ultrasonic Distance Sensor
  J1 = Basic Servo
  Sw2 = SS13D01
  R5 = Resistor [tolerance=±5% power=0.25 resistance=220 package=THT]
  R6 = Resistor [tolerance=±5% power=0.25 resistance=2.2k package=THT]
  R7 = Resistor [tolerance=±5% power=0.25 resistance=220 package=THT]
  R8 = Resistor [tolerance=±5% power=0.25 resistance=220 package=THT]
  Sw3 = SS13D01
  Sw4 = SS13D01
  R9 = Resistor [tolerance=±5% power=0.25 resistance=220 package=THT]
  R10 = Resistor [tolerance=±5% power=0.25 resistance=2.2k package=THT]
  R11 = Resistor [tolerance=±5% power=0.25 resistance=2.2k package=THT]
  R12 = Resistor [tolerance=±5% power=0.25 resistance=220 package=THT]
  R13 = Resistor [tolerance=±5% power=0.25 resistance=220 package=THT]
  R14 = Resistor [tolerance=±5% power=0.25 resistance=220 package=THT]
  R15 = Resistor [tolerance=±5% power=0.25 resistance=220 package=THT]
  R16 = Resistor [tolerance=±5% power=0.25 resistance=220 package=THT]
  U2 = POT [knob_status=50% power=0.5W package=pot_mammoth]
  U4 = POT [knob_status=50% power=0.5W package=pot_mammoth]
  Voltmeter1 = Voltmeter
  Voltmeter2 = Voltmeter

nets:
  GND: Part1.GND, R1.Pin_1, R4.Pin_1, U1.A, HC-SR04_Sensor_1.GND, J1.gnd, R6.Pin_1, R7.Pin_1, R10.Pin_1, R11.Pin_1, R13.Pin_1, R16.Pin_1, U2.A, U4.A, Voltmeter1.Com, Voltmeter2.Com
  N1: Part1.D4, HC-SR04_Sensor_1.ECHO
  N2: Part1.D5, HC-SR04_Sensor_1.TRIG
  N3: Part1.D9, J1.pulse
  N4: Part1.D10, Voltmeter2.Positive
  N5: Part1.D11/MOSI, Voltmeter1.Positive
  VCC: Part1.5V, Sw1.pin_1, R3.Pin_0, U1.E, HC-SR04_Sensor_1.VCC, J1.vcc, Sw2.pin_1, R5.Pin_0, Sw3.pin_1, Sw4.pin_1, R9.Pin_0, R15.Pin_0, U2.E, U4.E
  N6: Part1.A6, U4.S
  N7: Part1.A5, U2.S
  N8: Part1.A4, U1.S
  N9: Part1.A3, Sw3.pin_4, R10.Pin_0
  N10: Part1.A2, Sw4.pin_4, R11.Pin_0
  N11: Part1.A1, Sw2.pin_4, R6.Pin_0
  N12: Part1.A0, Sw1.pin_4, R4.Pin_0
  N13: Sw1.pin_2, R2.Pin_0, R3.Pin_1
  N14: Sw1.pin_3, R1.Pin_0, R2.Pin_1
  N15: Sw2.pin_2, R5.Pin_1, R8.Pin_0
  N16: Sw2.pin_3, R7.Pin_0, R8.Pin_1
  N17: Sw3.pin_2, R9.Pin_1, R12.Pin_0
  N18: Sw3.pin_3, R12.Pin_1, R16.Pin_0
  N19: Sw4.pin_2, R14.Pin_0, R15.Pin_1
  N20: Sw4.pin_3, R13.Pin_0, R14.Pin_1

custom parts:
  SS13D01: Side-actuated SPDT slide switch, as used on the Arduino Pro
  Voltmeter: A Standard Multimeter in Current mode
