# Fritzing sketch My-favourite-color-is-glitter (saved by Fritzing 0.9.9b)
breadboards: 1

parts:
  Part1 = Arduino Nano (Rev3.0)
  HC-SR04_Sensor_1 = HC-SR04 Ultrasonic Distance Sensor
  J1 = Basic Servo

nets:
  N1: Part1.D5, HC-SR04_Sensor_1.ECHO
  N2: Part1.D6, HC-SR04_Sensor_1.TRIG
  N3: Part1.D9, J1.pulse
  VCC: HC-SR04_Sensor_1.VCC, J1.vcc
  GND: HC-SR04_Sensor_1.GND, J1.gnd
